# Fritzing sketch quizboard_2_0 (saved by Fritzing 0.9.3b)
circuit board: 1.39778cm x 2.3706cm
circuit board: 8.46667cm x 5.64444cm
circuit board: 1.39778cm x 2.3706cm
breadboards: 3

parts:
  Bauteil1 = Arduino Uno (Rev3)
  LED_Shifter = HEF4094 [package="DIP16 [THT]"]
  R1 = Resistor [tolerance=±5% resistance=220 package=THT]
  R2 = Resistor [tolerance=±5% resistance=220 package=THT]
  R3 = Resistor [tolerance=±5% resistance=220 package=THT]
  R4 = Resistor [tolerance=±5% resistance=220 package=THT]
  R5 = Resistor [tolerance=±5% resistance=220 package=THT]
  R6 = Resistor [tolerance=±5% resistance=220 package=THT]
  R7 = Resistor [tolerance=±5% resistance=220 package=THT]
  R8 = Resistor [tolerance=±5% resistance=220 package=THT]
  LED_Stecker = male pin header, 9 pins [form="♂ (male)"]
  S1 = Pushbutton [package=THT]
  RE1 = Hexadecimal Rotary Encoder [part_number=APEM-PT65-303 package=THT]
  LED1 = LED - 5mm [color="Green (565nm)" package="5 mm [THT]"]
  LED2 = LED - 5mm [color="Green (560nm)" package="5 mm [THT]"]
  LED3 = LED - 5mm [color="Green (560nm)" package="5 mm [THT]"]
  LED4 = LED - 5mm [color="Green (565nm)" package="5 mm [THT]"]
  LED5 = LED - 5mm [color="Green (560nm)" package="5 mm [THT]"]
  LED6 = LED - 5mm [color="Green (565nm)" package="5 mm [THT]"]
  LED7 = LED - 5mm [color="Green (565nm)" package="5 mm [THT]"]
  LED8 = LED - 5mm [color="Green (560nm)" package="5 mm [THT]"]
  Hot_P_Shifter = HEF4094 [package="DIP16 [THT]"]
  Hot_Plugs = female pin header, 8 pins [form="♀ (female)"]
  Kont_B = rounded female pin header, 4 pins [form="♀ (female rounded)"]
  Kont_C = rounded female pin header, 4 pins [form="♀ (female rounded)"]
  R37 = Resistor [tolerance=±5% resistance=10M package=THT]
  Kont_A = rounded female pin header, 4 pins [form="♀ (female rounded)"]
  R38 = Resistor [tolerance=±5% resistance=10M package=THT]
  Kont_D = rounded female pin header, 4 pins [form="♀ (female rounded)"]
  R39 = Resistor [tolerance=±5% resistance=10M package=THT]
  R40 = Resistor [tolerance=±5% resistance=10M package=THT]
  Sensor_Buchse = female pin header, 4 pins [form="♀ (female)"]
  LED_Buchse = rounded female pin header, 9 pins [form="♀ (female rounded)"]
  R20 = Resistor [tolerance=±5% resistance=1M package=THT]
  R19 = Resistor [tolerance=±5% resistance=1M package=THT]
  R18 = Resistor [tolerance=±5% resistance=1M package=THT]
  R17 = Resistor [tolerance=±5% resistance=1M package=THT]
  R32 = Resistor [tolerance=±5% resistance=1M package=THT]
  R36 = Resistor [tolerance=±5% resistance=1M package=THT]
  R34 = Resistor [tolerance=±5% resistance=1M package=THT]
  R35 = Resistor [tolerance=±5% resistance=1M package=THT]
  R31 = Resistor [tolerance=±5% resistance=1M package=THT]
  R30 = Resistor [tolerance=±5% resistance=1M package=THT]
  R33 = Resistor [tolerance=±5% resistance=1M package=THT]
  R25 = Resistor [tolerance=±5% resistance=1M package=THT]
  7_Segment1 = 7 Segment Display  # not connected

nets:
  N1: Bauteil1.A0, R37.Pin_1, Kont_A.pin1, Sensor_Buchse.pin4, R17.Pin_0, R33.Pin_1
  N2: Bauteil1.A1, Kont_B.pin1, R38.Pin_1, Sensor_Buchse.pin3, R18.Pin_0, R30.Pin_1
  N3: Bauteil1.A2, Kont_C.pin1, R39.Pin_1, Sensor_Buchse.pin2, R19.Pin_0, R31.Pin_1
  N4: Bauteil1.A3, Kont_D.pin1, R40.Pin_1, Sensor_Buchse.pin1, R20.Pin_0, R32.Pin_1
  N5: Bauteil1.D9_PWM, RE1.Output4Pin
  N6: Bauteil1.D10_PWM/SS, RE1.Output1Pin
  N7: Bauteil1.D11_PWM/MOSI, RE1.Output8pin
  N8: Bauteil1.D12/MISO, RE1.Output2Pin
  N9: Bauteil1.D13/SCK, S1.leg0
  N10: Bauteil1.D0/RX, LED_Shifter.CLOCK
  N11: Bauteil1.D1/TX, LED_Shifter.DATA
  N12: Bauteil1.D2, LED_Shifter.STROBE
  N13: Bauteil1.D3_PWM, Hot_P_Shifter.CLOCK
  N14: Bauteil1.D4, Hot_P_Shifter.DATA
  N15: Bauteil1.D5_PWM, Hot_P_Shifter.STROBE
  VDD: Bauteil1.5V, LED_Shifter.OE, LED_Shifter.Vdd, S1.leg1, RE1.InputCommon, RE1.InputCommon2, Hot_P_Shifter.OE, Hot_P_Shifter.Vdd
  VSS: Bauteil1.GND, LED_Shifter.Vss, LED_Stecker.pin1, LED1.anode, LED2.anode, LED3.anode, LED4.anode, LED5.anode, LED6.anode, LED7.anode, LED8.anode, Hot_P_Shifter.Vss, LED_Buchse.pin1, R20.Pin_1, R19.Pin_1, R18.Pin_1, R17.Pin_1
  N16: LED_Shifter.Q1, R1.Pin_1
  N17: LED_Shifter.Q2, R2.Pin_1
  N18: LED_Shifter.Q3, R3.Pin_1
  N19: LED_Shifter.Q4, R4.Pin_1
  N20: LED_Shifter.Q8, R7.Pin_1
  N21: LED_Shifter.Q7, R8.Pin_1
  N22: LED_Shifter.Q6, R6.Pin_1
  N23: LED_Shifter.Q5, R5.Pin_1
  N24: R1.Pin_0, LED_Stecker.pin9, LED8.cathode, LED_Buchse.pin9
  N25: R2.Pin_0, LED_Stecker.pin8, LED7.cathode, LED_Buchse.pin8
  N26: R3.Pin_0, LED_Stecker.pin7, LED6.cathode, LED_Buchse.pin7
  N27: R4.Pin_0, LED_Stecker.pin6, LED5.cathode, LED_Buchse.pin6
  N28: R5.Pin_0, LED_Stecker.pin5, LED4.cathode, LED_Buchse.pin5
  N29: R6.Pin_0, LED_Stecker.pin4, LED3.cathode, LED_Buchse.pin4
  N30: R7.Pin_0, LED_Stecker.pin2, LED1.cathode, LED_Buchse.pin2
  N31: R8.Pin_0, LED_Stecker.pin3, LED2.cathode, LED_Buchse.pin3
  N32: Hot_P_Shifter.Q1, Hot_Plugs.pin1
  N33: Hot_P_Shifter.Q2, Hot_Plugs.pin2
  N34: Hot_P_Shifter.Q3, Hot_Plugs.pin3
  N35: Hot_P_Shifter.Q4, Hot_Plugs.pin4
  N36: Hot_P_Shifter.Q8, Hot_Plugs.pin8
  N37: Hot_P_Shifter.Q7, Hot_Plugs.pin7
  N38: Hot_P_Shifter.Q6, Hot_Plugs.pin6
  N39: Hot_P_Shifter.Q5, Hot_Plugs.pin5
  N40: Kont_B.pin2, R34.Pin_0, R30.Pin_0
  N41: Kont_B.pin3, R34.Pin_1
  N42: Kont_B.pin4, R38.Pin_0
  N43: Kont_C.pin2, R35.Pin_0, R31.Pin_0
  N44: Kont_C.pin3, R35.Pin_1
  N45: Kont_C.pin4, R39.Pin_0
  N46: R37.Pin_0, Kont_A.pin4
  N47: Kont_A.pin2, R33.Pin_0, R25.Pin_0
  N48: Kont_A.pin3, R25.Pin_1
  N49: Kont_D.pin2, R32.Pin_0, R36.Pin_0
  N50: Kont_D.pin3, R36.Pin_1
  N51: Kont_D.pin4, R40.Pin_0
